// Digital circuit fourBitAdder.dig as structural Verilog
module fourBitAdder (
  input  [3:0] in_a,
  input  [3:0] in_b,
  input  c_in,
  output c_out,
  output [3:0] out
);

  wire fulladder_2_c_out, fulladder_3_c_out, fulladder_4_c_out;

  fullAdder fulladder_1 (.in_a(in_a[3]), .in_b(in_b[3]), .c_in(fulladder_2_c_out), .c_out(c_out), .sum(out[3]));
  fullAdder fulladder_2 (
    .in_a(in_a[2]), .in_b(in_b[2]), .c_in(fulladder_3_c_out), .c_out(fulladder_2_c_out), .sum(out[2]));
  fullAdder fulladder_3 (
    .in_a(in_a[1]), .in_b(in_b[1]), .c_in(fulladder_4_c_out), .c_out(fulladder_3_c_out), .sum(out[1]));
  fullAdder fulladder_4 (.in_a(in_a[0]), .in_b(in_b[0]), .c_in(c_in), .c_out(fulladder_4_c_out), .sum(out[0]));
endmodule
