// Digital circuit fullAdder.dig as structural Verilog
module fullAdder (
  input  in_a,
  input  in_b,
  input  c_in,
  output c_out,
  output sum
);

  wire and_1_out, and_2_out, and_3_out;

  xor xor_1 (sum, in_a, in_b, c_in);
  and and_1 (and_1_out, c_in, in_b);
  and and_2 (and_2_out, c_in, in_a);
  and and_3 (and_3_out, in_b, in_a);
  or or_1 (c_out, and_1_out, and_2_out, and_3_out);
endmodule
