// Digital circuit sixteenBitAdder.dig as structural Verilog
module sixteenBitAdder (
  input  [15:0] in_a,
  input  [15:0] in_b,
  input  c_in,
  output [15:0] out,
  output over,
  output c_out
);

  wire fourbitadder_2_c_out, fourbitadder_3_c_out, fourbitadder_4_c_out;

  fourBitAdder fourbitadder_1 (
    .in_a(in_a[15:12]), .in_b(in_b[15:12]), .c_in(fourbitadder_2_c_out), .c_out(c_out), .out(out[15:12]));
  fourBitAdder fourbitadder_2 (
    .in_a(in_a[11:8]), .in_b(in_b[11:8]), .c_in(fourbitadder_3_c_out), .c_out(fourbitadder_2_c_out),
    .out(out[11:8]));
  fourBitAdder fourbitadder_3 (
    .in_a(in_a[7:4]), .in_b(in_b[7:4]), .c_in(fourbitadder_4_c_out), .c_out(fourbitadder_3_c_out),
    .out(out[7:4]));
  fourBitAdder fourbitadder_4 (
    .in_a(in_a[3:0]), .in_b(in_b[3:0]), .c_in(c_in), .c_out(fourbitadder_4_c_out), .out(out[3:0]));
  xor xor_1 (over, c_out, fourbitadder_2_c_out);
endmodule
