// Digital circuit fourBitIncrementer.dig as structural Verilog
module fourBitIncrementer (
  input  [3:0] a,
  input  inc,
  output cry,
  output [3:0] y
);

  wire halfadder_2_carry, halfadder_3_carry, halfadder_4_carry;

  halfAdder halfadder_1 (.in_a(a[3]), .in_b(halfadder_2_carry), .sum(y[3]), .carry(cry));
  halfAdder halfadder_2 (.in_a(a[2]), .in_b(halfadder_3_carry), .sum(y[2]), .carry(halfadder_2_carry));
  halfAdder halfadder_3 (.in_a(a[1]), .in_b(halfadder_4_carry), .sum(y[1]), .carry(halfadder_3_carry));
  halfAdder halfadder_4 (.in_a(a[0]), .in_b(inc), .sum(y[0]), .carry(halfadder_4_carry));
endmodule
