// Digital circuit programCounter.dig as structural Verilog
module programCounter (
  input  enable,
  input  reset,
  input  clk,
  output [7:0] q
);

  wire sixteenbitincrementer_1_p3;

  // sixteenBitIncrementer sixteenbitincrementer_1: pin names not known; wires that end beside it: q, 1'b1, sixteenbitincrementer_1_p3
  // sixteenBitReg sixteenbitreg_1: pin names not known; wires that end beside it: sixteenbitincrementer_1_p3, enable, clk, reset, q
endmodule
