// Digital circuit sixteenBitIncrementer.dig as structural Verilog
module sixteenBitIncrementer (
  input  [15:0] in,
  input  inc,
  output carry,
  output [15:0] out
);

  wire halfadder_1_carry, halfadder_2_carry, halfadder_3_carry, halfadder_4_carry, halfadder_5_carry,
       halfadder_6_carry, halfadder_7_carry, halfadder_8_carry, halfadder_9_carry, halfadder_10_carry,
       halfadder_11_carry, halfadder_12_carry, halfadder_13_carry, halfadder_14_carry, halfadder_15_carry;

  halfAdder halfadder_1 (.in_a(inc), .in_b(in[0]), .sum(out[0]), .carry(halfadder_1_carry));
  halfAdder halfadder_2 (.in_a(halfadder_1_carry), .in_b(in[1]), .sum(out[1]), .carry(halfadder_2_carry));
  halfAdder halfadder_3 (.in_a(halfadder_2_carry), .in_b(in[2]), .sum(out[2]), .carry(halfadder_3_carry));
  halfAdder halfadder_4 (.in_a(halfadder_3_carry), .in_b(in[3]), .sum(out[3]), .carry(halfadder_4_carry));
  halfAdder halfadder_5 (.in_a(halfadder_4_carry), .in_b(in[4]), .sum(out[4]), .carry(halfadder_5_carry));
  halfAdder halfadder_6 (.in_a(halfadder_5_carry), .in_b(in[5]), .sum(out[5]), .carry(halfadder_6_carry));
  halfAdder halfadder_7 (.in_a(halfadder_6_carry), .in_b(in[6]), .sum(out[6]), .carry(halfadder_7_carry));
  halfAdder halfadder_8 (.in_a(halfadder_7_carry), .in_b(in[7]), .sum(out[7]), .carry(halfadder_8_carry));
  halfAdder halfadder_9 (.in_a(halfadder_8_carry), .in_b(in[8]), .sum(out[8]), .carry(halfadder_9_carry));
  halfAdder halfadder_10 (.in_a(halfadder_9_carry), .in_b(in[9]), .sum(out[9]), .carry(halfadder_10_carry));
  halfAdder halfadder_11 (.in_a(halfadder_10_carry), .in_b(in[10]), .sum(out[10]), .carry(halfadder_11_carry));
  halfAdder halfadder_12 (.in_a(halfadder_11_carry), .in_b(in[11]), .sum(out[11]), .carry(halfadder_12_carry));
  halfAdder halfadder_13 (.in_a(halfadder_12_carry), .in_b(in[12]), .sum(out[12]), .carry(halfadder_13_carry));
  halfAdder halfadder_14 (.in_a(halfadder_13_carry), .in_b(in[13]), .sum(out[13]), .carry(halfadder_14_carry));
  halfAdder halfadder_15 (.in_a(halfadder_14_carry), .in_b(in[14]), .sum(out[14]), .carry(halfadder_15_carry));
  halfAdder halfadder_16 (.in_a(halfadder_15_carry), .in_b(in[15]), .sum(out[15]), .carry(carry));
endmodule
