// Digital circuit andAdd.dig as structural Verilog
module andAdd (
  input  [15:0] in_a,
  input  [15:0] in_b,
  input  cin,
  input  add,
  input  pass,
  output [15:0] out,
  output c_out,
  output over
);

  wire [15:0] sixteenbitadder_1_out, sixteenbitand_1_out, sixteenbitmux_1_out;

  sixteenBitAnd sixteenbitand_1 (.in_a(in_a), .in_b(in_b), .out(sixteenbitand_1_out));
  sixteenBitAdder sixteenbitadder_1 (
    .in_a(in_a), .in_b(in_b), .c_in(cin), .out(sixteenbitadder_1_out), .over(over), .c_out(c_out));
  sixteenBitMux sixteenbitmux_1 (
    .in_a(sixteenbitand_1_out), .in_b(sixteenbitadder_1_out), .sel(add), .out(sixteenbitmux_1_out));
  sixteenBitMux sixteenbitmux_2 (.in_a(sixteenbitmux_1_out), .in_b(in_a), .sel(pass), .out(out));
endmodule
