// Digital circuit fourBitAnd.dig as structural Verilog
module fourBitAnd (
  input  [3:0] in_a,
  input  [3:0] in_b,
  output [3:0] out
);

  and and_1 (out[3], in_a[3], in_b[3]);
  and and_2 (out[2], in_a[2], in_b[2]);
  and and_3 (out[1], in_a[1], in_b[1]);
  and and_4 (out[0], in_a[0], in_b[0]);
endmodule
