// Digital circuit notNeg.dig as structural Verilog
module notNeg (
  input  [15:0] in,
  input  invert,
  input  neg,
  output [15:0] out,
  output carry
);

  wire and_1_out;
  wire [15:0] xor_12_out;

  xor xor_1 (xor_12_out[0], in[0], invert);
  xor xor_2 (xor_12_out[1], in[1], invert);
  xor xor_3 (xor_12_out[2], in[2], invert);
  xor xor_4 (xor_12_out[3], in[3], invert);
  xor xor_5 (xor_12_out[4], in[4], invert);
  xor xor_6 (xor_12_out[5], in[5], invert);
  xor xor_7 (xor_12_out[6], in[6], invert);
  xor xor_8 (xor_12_out[7], in[7], invert);
  xor xor_9 (xor_12_out[8], in[8], invert);
  xor xor_10 (xor_12_out[9], in[9], invert);
  xor xor_11 (xor_12_out[10], in[10], invert);
  xor xor_12 (xor_12_out[11], in[11], invert);
  xor xor_13 (xor_12_out[12], in[12], invert);
  xor xor_14 (xor_12_out[13], in[13], invert);
  xor xor_15 (xor_12_out[14], in[14], invert);
  xor xor_16 (xor_12_out[15], in[15], invert);
  and and_1 (and_1_out, invert, neg);
  sixteenBitIncrementer sixteenbitincrementer_1 (.in(xor_12_out), .inc(and_1_out), .carry(carry), .out(out));
endmodule
