// Digital circuit sixteenBitAnd.dig as structural Verilog
module sixteenBitAnd (
  input  [15:0] in_a,
  input  [15:0] in_b,
  output [15:0] out
);

  fourBitAnd fourbitand_1 (.in_a(in_a[15:12]), .in_b(in_b[15:12]), .out(out[15:12]));
  fourBitAnd fourbitand_2 (.in_a(in_a[11:8]), .in_b(in_b[11:8]), .out(out[11:8]));
  fourBitAnd fourbitand_3 (.in_a(in_a[7:4]), .in_b(in_b[7:4]), .out(out[7:4]));
  fourBitAnd fourbitand_4 (.in_a(in_a[3:0]), .in_b(in_b[3:0]), .out(out[3:0]));
endmodule
