// Digital circuit zeroChecker.dig as structural Verilog
module zeroChecker (
  input  [15:0] in,
  output out
);

  wire or_1_out, or_2_out, or_3_out, or_4_out, or_5_out, or_6_out, or_7_out, or_8_out, or_9_out, or_10_out,
       or_11_out, or_12_out, or_13_out, or_14_out, or_15_out;

  or or_1 (or_1_out, in[15], in[14]);
  or or_2 (or_2_out, in[13], in[12]);
  or or_3 (or_3_out, in[11], in[10]);
  or or_4 (or_4_out, in[9], in[8]);
  or or_5 (or_5_out, in[7], in[6]);
  or or_6 (or_6_out, in[5], in[4]);
  or or_7 (or_7_out, in[3], in[2]);
  or or_8 (or_8_out, in[1], in[0]);
  or or_9 (or_9_out, or_1_out, or_2_out);
  or or_10 (or_10_out, or_3_out, or_4_out);
  or or_11 (or_11_out, or_5_out, or_6_out);
  or or_12 (or_12_out, or_7_out, or_8_out);
  or or_13 (or_13_out, or_9_out, or_10_out);
  or or_14 (or_14_out, or_11_out, or_12_out);
  or or_15 (or_15_out, or_13_out, or_14_out);
  not not_1 (out, or_15_out);
endmodule
