// Digital circuit eightBitMux.dig as structural Verilog
module eightBitMux (
  input  [7:0] in_a,
  input  [7:0] in_b,
  input  sel,
  output [7:0] out
);

  fourBitMux fourbitmux_1 (.in_a(in_a[7:4]), .in_b(in_b[7:4]), .sel(sel), .out(out[7:4]));
  fourBitMux fourbitmux_2 (.in_a(in_a[3:0]), .in_b(in_b[3:0]), .sel(sel), .out(out[3:0]));
endmodule
