// Digital circuit sixteenBitMux.dig as structural Verilog
module sixteenBitMux (
  input  [15:0] in_a,
  input  [15:0] in_b,
  input  sel,
  output [15:0] out
);

  fourBitMux fourbitmux_1 (.in_a(in_a[3:0]), .in_b(in_b[3:0]), .sel(sel), .out(out[3:0]));
  fourBitMux fourbitmux_2 (.in_a(in_a[7:4]), .in_b(in_b[7:4]), .sel(sel), .out(out[7:4]));
  fourBitMux fourbitmux_3 (.in_a(in_a[11:8]), .in_b(in_b[11:8]), .sel(sel), .out(out[11:8]));
  fourBitMux fourbitmux_4 (.in_a(in_a[15:12]), .in_b(in_b[15:12]), .sel(sel), .out(out[15:12]));
endmodule
