// Digital circuit twoBitBusMux.dig as structural Verilog
module twoBitBusMux (
  input  [1:0] in_a,
  input  [1:0] in_b,
  input  sel,
  output [1:0] out
);

  twoBitMux twobitmux_1 (.in_a(in_a[0]), .in_b(in_b[0]), .sel(sel), .out(out[0]));
  twoBitMux twobitmux_2 (.in_a(in_a[1]), .in_b(in_b[1]), .sel(sel), .out(out[1]));
endmodule
