// Digital circuit twoBitMux.dig as structural Verilog
module twoBitMux (
  input  in_a,
  input  in_b,
  input  sel,
  output out
);

  wire and_1_out, and_2_out, not_1_out;

  and and_1 (and_1_out, in_a, not_1_out);
  not not_1 (not_1_out, sel);
  and and_2 (and_2_out, in_b, sel);
  or or_1 (out, and_1_out, and_2_out);
endmodule
