// Digital circuit fourBitReg.dig as structural Verilog
module fourBitReg (
  input  [3:0] d,
  input  enable,
  input  reset,
  input  clk,
  output [3:0] q
);

  wire [3:0] fourbitmux_1_out;

  fourBitMux fourbitmux_1 (.in_a(q), .in_b(d), .sel(enable), .out(fourbitmux_1_out));
  D_FF_AS d_ff_as_1 (.Set(1'b0), .D(fourbitmux_1_out[0]), .C(clk), .Clr(reset), .Q(q[0]));  // open: nQ
  D_FF_AS d_ff_as_2 (.Set(1'b0), .D(fourbitmux_1_out[1]), .C(clk), .Clr(reset), .Q(q[1]));  // open: nQ
  D_FF_AS d_ff_as_3 (.Set(1'b0), .D(fourbitmux_1_out[2]), .C(clk), .Clr(reset), .Q(q[2]));  // open: nQ
  D_FF_AS d_ff_as_4 (.Set(1'b0), .D(fourbitmux_1_out[3]), .C(clk), .Clr(reset), .Q(q[3]));  // open: nQ
endmodule
