// Digital circuit sixBitReg.dig as structural Verilog
module sixBitReg (
  input  [5:0] in,
  input  sel,
  input  clk,
  input  clr,
  output [5:0] out
);

  wire [7:0] sixbitmux_1_out;

  sixBitMux sixbitmux_1 (.in_a(out), .in_b(in), .sel(sel), .out(sixbitmux_1_out));
  D_FF_AS d_ff_as_1 (.Set(1'b0), .D(sixbitmux_1_out[0]), .C(clk), .Clr(clr), .Q(out[0]));  // open: nQ
  D_FF_AS d_ff_as_2 (.Set(1'b0), .D(sixbitmux_1_out[1]), .C(clk), .Clr(clr), .Q(out[1]));  // open: nQ
  D_FF_AS d_ff_as_3 (.Set(1'b0), .D(sixbitmux_1_out[2]), .C(clk), .Clr(clr), .Q(out[2]));  // open: nQ
  D_FF_AS d_ff_as_4 (.Set(1'b0), .D(sixbitmux_1_out[3]), .C(clk), .Clr(clr), .Q(out[3]));  // open: nQ
  D_FF_AS d_ff_as_5 (.Set(1'b0), .D(sixbitmux_1_out[4]), .C(clk), .Clr(clr), .Q(out[4]));  // open: nQ
  D_FF_AS d_ff_as_6 (.Set(1'b0), .D(sixbitmux_1_out[5]), .C(clk), .Clr(clr), .Q(out[5]));  // open: nQ
endmodule
