// Digital circuit sixteenBitReg.dig as structural Verilog
module sixteenBitReg (
  input  [15:0] in,
  input  enable,
  input  clr,
  input  clk,
  output [15:0] out
);

  wire [15:0] sixteenbitmux_1_out;

  sixteenBitMux sixteenbitmux_1 (.in_a(out), .in_b(in), .sel(enable), .out(sixteenbitmux_1_out));
  D_FF_AS d_ff_as_1 (.Set(1'b0), .D(sixteenbitmux_1_out[0]), .C(clk), .Clr(clr), .Q(out[0]));  // open: nQ
  D_FF_AS d_ff_as_2 (.Set(1'b0), .D(sixteenbitmux_1_out[1]), .C(clk), .Clr(clr), .Q(out[1]));  // open: nQ
  D_FF_AS d_ff_as_3 (.Set(1'b0), .D(sixteenbitmux_1_out[2]), .C(clk), .Clr(clr), .Q(out[2]));  // open: nQ
  D_FF_AS d_ff_as_4 (.Set(1'b0), .D(sixteenbitmux_1_out[3]), .C(clk), .Clr(clr), .Q(out[3]));  // open: nQ
  D_FF_AS d_ff_as_5 (.Set(1'b0), .D(sixteenbitmux_1_out[4]), .C(clk), .Clr(clr), .Q(out[4]));  // open: nQ
  D_FF_AS d_ff_as_6 (.Set(1'b0), .D(sixteenbitmux_1_out[5]), .C(clk), .Clr(clr), .Q(out[5]));  // open: nQ
  D_FF_AS d_ff_as_7 (.Set(1'b0), .D(sixteenbitmux_1_out[6]), .C(clk), .Clr(clr), .Q(out[6]));  // open: nQ
  D_FF_AS d_ff_as_8 (.Set(1'b0), .D(sixteenbitmux_1_out[7]), .C(clk), .Clr(clr), .Q(out[7]));  // open: nQ
  D_FF_AS d_ff_as_9 (.Set(1'b0), .D(sixteenbitmux_1_out[8]), .C(clk), .Clr(clr), .Q(out[8]));  // open: nQ
  D_FF_AS d_ff_as_10 (.Set(1'b0), .D(sixteenbitmux_1_out[9]), .C(clk), .Clr(clr), .Q(out[9]));  // open: nQ
  D_FF_AS d_ff_as_11 (.Set(1'b0), .D(sixteenbitmux_1_out[10]), .C(clk), .Clr(clr), .Q(out[10]));  // open: nQ
  D_FF_AS d_ff_as_12 (.Set(1'b0), .D(sixteenbitmux_1_out[11]), .C(clk), .Clr(clr), .Q(out[11]));  // open: nQ
  D_FF_AS d_ff_as_13 (.Set(1'b0), .D(sixteenbitmux_1_out[12]), .C(clk), .Clr(clr), .Q(out[12]));  // open: nQ
  D_FF_AS d_ff_as_14 (.Set(1'b0), .D(sixteenbitmux_1_out[13]), .C(clk), .Clr(clr), .Q(out[13]));  // open: nQ
  D_FF_AS d_ff_as_15 (.Set(1'b0), .D(sixteenbitmux_1_out[14]), .C(clk), .Clr(clr), .Q(out[14]));  // open: nQ
  D_FF_AS d_ff_as_16 (.Set(1'b0), .D(sixteenbitmux_1_out[15]), .C(clk), .Clr(clr), .Q(out[15]));  // open: nQ
endmodule
