// Digital circuit twoBitReg.dig as structural Verilog
module twoBitReg (
  input  [1:0] in,
  input  enable,
  input  clr,
  input  clk,
  output [1:0] out
);

  wire [1:0] twobitbusmux_1_out;

  twoBitBusMux twobitbusmux_1 (.in_a(out), .in_b(in), .sel(enable), .out(twobitbusmux_1_out));
  D_FF_AS d_ff_as_1 (.Set(1'b0), .D(twobitbusmux_1_out[0]), .C(clk), .Clr(clr), .Q(out[0]));  // open: nQ
  D_FF_AS d_ff_as_2 (.Set(1'b0), .D(twobitbusmux_1_out[1]), .C(clk), .Clr(clr), .Q(out[1]));  // open: nQ
endmodule
