// Digital circuit alu.dig as structural Verilog
module alu (
  input  [15:0] in_b,
  input  invert,
  input  c_in,
  input  arith,
  input  pass,
  input  [15:0] in_a,
  output [15:0] out,
  output c_out,
  output over
);

  wire notneg_1_carry;
  wire [15:0] notneg_1_out;

  notNeg notneg_1 (.in(in_a), .invert(invert), .neg(arith), .out(notneg_1_out), .carry(notneg_1_carry));
  andAdd andadd_1 (
    .in_a(notneg_1_out), .in_b(in_b), .cin(c_in), .add(arith), .pass(pass), .out(out), .c_out(c_out),
    .over(over));
  // also tied to GND on the sheet: notneg_1_carry
endmodule
