// Digital circuit controller.dig as structural Verilog
module controller (
  input  clk,
  input  clr,
  input  [7:0] data_in,
  input  load__ir,
  output [9:0] control
);

  wire [1:0] step__reg;
  wire [7:0] instr__reg;
  wire [13:10] rom__out;

  eightBitReg eightbitreg_1 (.in(data_in), .sel(load__ir), .clk(clk), .clr(clr), .out(instr__reg));
  // twoBitReg twobitreg_1: pin names not known; wires that end beside it: rom__out[13:12], 1'b1, clk, clr, step__reg
  ROM #(.AddrBits(10), .Bits(14)) microcode_ROM (.A({instr__reg, step__reg}), .sel(1'b1), .D({rom__out, control}));

  // Other names for the same wires on the sheet: rom__out[9:0] = control

  // Notes on the sheet:
  //   contents of microcode_ROM (hex, n*v repeats v):
  //   1224,2001,0,0,1224,2001,3120,34,1224,2001,3100,a,1224,2001,3030
  //   ,0,1224,2001,3100,94,1224,2001,3100,d4,1224,2001,3100,14,1224
  //   ,2001,3070,0,1224,2001,30c8,a,1224,2001,3100,0,1224,2001,3030
  //   ,0,1224,2001,3028
endmodule
