// Digital circuit fourBitMux.dig as structural Verilog
module fourBitMux (
  input  [3:0] in_a,
  input  [3:0] in_b,
  input  sel,
  output [3:0] out
);

  twoBitMux twobitmux_1 (.in_a(in_a[0]), .in_b(in_b[0]), .sel(sel), .out(out[0]));
  twoBitMux twobitmux_2 (.in_a(in_a[1]), .in_b(in_b[1]), .sel(sel), .out(out[1]));
  twoBitMux twobitmux_3 (.in_a(in_a[2]), .in_b(in_b[2]), .sel(sel), .out(out[2]));
  twoBitMux twobitmux_4 (.in_a(in_a[3]), .in_b(in_b[3]), .sel(sel), .out(out[3]));
endmodule
