// Digital circuit microprocessor.dig as structural Verilog
module microprocessor (
  input  clk,
  input  [15:0] in,
  input  reset,
  output [15:0] accum
);

  wire [7:0] sixteenbitbrainless_1_data_bus;
  wire [9:0] controller_1_control;
  wire [15:0] addressgen_1_addr__bus;
  wire [15:8] sixteenbitbrainless_1_data_bus_2;

  addressGen addressgen_1 (
    .data__bus({sixteenbitbrainless_1_data_bus_2, sixteenbitbrainless_1_data_bus}), .clk(clk), .reset(reset),
    .use__pc(controller_1_control[9]), .load__mar(controller_1_control[8]), .addr__bus(addressgen_1_addr__bus));
  controller controller_1 (
    .clk(clk), .clr(reset), .data_in(sixteenbitbrainless_1_data_bus), .load__ir(controller_1_control[0]),
    .control(controller_1_control));
  sixteenBitBrainless sixteenbitbrainless_1 (
    .addr__bus(addressgen_1_addr__bus), .data_in(in), .arith(controller_1_control[7]),
    .invert(controller_1_control[6]), .pass(controller_1_control[5]), .load__accum(controller_1_control[4]),
    .accum__gt_bus(controller_1_control[3]), .write(controller_1_control[2]), .read(controller_1_control[1]),
    .clk(clk), .clr(reset), .accum(accum),
    .data_bus({sixteenbitbrainless_1_data_bus_2, sixteenbitbrainless_1_data_bus}));
endmodule
