// Digital circuit programRam.dig as structural Verilog
module programRam (
  input  [15:0] addr,
  input  [15:0] data_in,
  input  clk,
  input  write,
  output [15:0] data_out
);

  RAMDualPort #(.AddrBits(16), .isProgramMemory("true"), .Bits(16)) program_ram (
    .A(addr), .Din(data_in), .str(write), .C(clk), .ld(1'b1), .D(data_out));
endmodule
