// Digital circuit sixteenBitBrainless.dig as structural Verilog
module sixteenBitBrainless (
  input  [15:0] addr__bus,
  input  [15:0] data_in,
  input  arith,
  input  invert,
  input  pass,
  input  load__accum,
  input  accum__gt_bus,
  input  write,
  input  read,
  input  clk,
  input  clr,
  output [15:0] accum,
  output [15:0] data_bus
);

  wire [15:0] alu_1_p7, programram_1_data_out, sixteenbitmux_2_out;

  // alu alu_1: pin names not known; wires that end beside it: accum, invert, 1'b0, arith, pass, data_bus, alu_1_p7
  sixteenBitReg sixteenbitreg_1 (.in(alu_1_p7), .sel(load__accum), .clr(clr), .clk(clk), .out(accum));
  sixteenBitMux sixteenbitmux_1 (.in_a(sixteenbitmux_2_out), .in_b(accum), .sel(accum__gt_bus), .out(data_bus));
  programRam programram_1 (
    .addr(addr__bus), .data_in(data_bus), .clk(clk), .write(write), .data_out(programram_1_data_out));
  sixteenBitMux sixteenbitmux_2 (.in_a(data_in), .in_b(programram_1_data_out), .sel(read), .out(sixteenbitmux_2_out));
endmodule
