// Digital circuit halfAdder.dig as structural Verilog
module halfAdder (
  input  in_a,
  input  in_b,
  output sum,
  output carry
);

  xor xor_1 (sum, in_a, in_b);
  and and_1 (carry, in_a, in_b);
endmodule
